# Fritzing sketch silvia_brew_control (saved by Fritzing 0.9.3b)
breadboards: 1

parts:
  Part1 = Arduino Uno (Rev3)
  D2425D1 = Crydom D2425D
  R3 = Resistor [tolerance=±5% resistance=10k package=THT]
  Brew_Switch = SPST Switch [package=r_sw_th]
  Raspberry_Pi_1 = Raspberry Pi 3 [part_number=RPI-3-V1.2]

nets:
  N1: Part1.D12/MISO, D2425D1.A+, D2425D1.B+, R3.Pin_0
  GND: Part1.GND, D2425D1.A-, D2425D1.B-, R3.Pin_1, Brew_Switch.P, Raspberry_Pi_1.GND
  N2: Brew_Switch.O, Raspberry_Pi_1.GIPO27, Raspberry_Pi_1.ID_SC

notes:
  Live
  Solenoid
  Neutral
  Pump

custom parts:
  Crydom D2425D: Crydom dual solid state relay Input 4-15 VDC Output 120/240 VAC 25A
