# Fritzing sketch silvia_oled_display (saved by Fritzing 0.9.3b)
breadboards: 1

parts:
  Part1 = Arduino Uno (Rev3)
  OLED2 = OLED 128x64 I2C Monochrome Display

nets:
  N1: Part1.A4/SDA, OLED2.SDA
  N2: Part1.A5/SCL, OLED2.SCK
  GND: Part1.GND, OLED2.GND
  5V: Part1.5V, OLED2.VDD
