# Fritzing sketch silvia_temperature_control (saved by Fritzing 0.9.3b)
breadboards: 1

parts:
  Part1 = Arduino Uno (Rev3)
  LM35DT2 = LM35DT [package="TO220 [THT]"]
  SSR2 = Generic SSR
  R2 = Resistor [tolerance=±5% resistance=10k package=THT]

nets:
  N1: Part1.A0, LM35DT2.GND
  N2: Part1.D13/SCK, SSR2.input+, R2.Pin_0
  N3: Part1.GND, LM35DT2.Vout, SSR2.Input-, R2.Pin_1
  N4: Part1.5V, LM35DT2.+Vs

custom parts:
  LM35DT: A LM35 temperature sensor with a temperature range from -55°C to 150°C.
  Generic SSR: Generic solid state relay. Input 3-32VDC Output 24-440VAC 25A
